# Fritzing sketch Sketch (saved by Fritzing 0.9.5d)

parts:
  Part1 = Arduino Nano (Rev3.0) (ICSP)
  VCC1 = Battery
  VCC2 = Battery
  A1 = MH-FMD buzzer
  LCD2004-I2C1 = LCD2004-I2C
  A2 = AMS11176 module
  Joystick_KY-1 = Joystick KY-023
  SW1 = Slide_Switch_new

nets:
  N1: Part1.D3, Joystick_KY-1.pin1
  N2: Part1.D4, A1.Pin_2
  N3: Part1.D9, A1.Pin_1
  GND: Part1.GND, VCC2.-, A1.Pin_3, LCD2004-I2C1.GND, Joystick_KY-1.pin5, SW1.pin_2
  5V: Part1.5V, LCD2004-I2C1.VCC, A2.pin2, Joystick_KY-1.pin4
  N4: Part1.A5, LCD2004-I2C1.SCL
  N5: Part1.A4, LCD2004-I2C1.SDA
  N6: Part1.A1, Joystick_KY-1.pin2
  N7: Part1.A0, Joystick_KY-1.pin3
  N8: VCC1.+, A2.pin1
  N9: A2.pin3, SW1.pin_1

notes:
  5V Regulator

custom parts:
  MH-FMD buzzer: MH-FMD buzzer.
  LCD2004-I2C: A standard character display with 4x20 characters. Comes in many colors with LCM2004 IIC attached.
  AMS11176 module: DC-DC step-down modules ( input DC 4.5～7V , output DC 3.3V ).
  Slide_Switch_new: the New two pin slide switch
